// Logisim project Processor.circ as structural Verilog: 10 circuits, main circuit Processor
module Processor (
  input  Reset,
  input  [3:0] Display_Address
);

  wire alu_1_is, alu_1_is_2, and_1_out, Branch, Clock, flags_1_flags_e, flags_1_flags_gt, isBeq, isBeq_2_q,
       isBeq_3_q, isBeq_q, isBgt, isBgt_2_q, isBgt_3_q, isBgt_q, isCall, isCall_2_q, isCall_q, isImmediate,
       isImmediate_2_q, isImmediate_q, isLd, isLD_2_q, isLD_q, IsldUse, IsRet, isRet_2_q, isRet_3_q, isRet_q,
       isSt, isSt_2_q, isSt_3_q, isSt_q, isUBranch, isUBranch_2_q, isUBranch_3_q, isUBranch_q, IsWb,
       isWb_2_q, isWb_3_q, isWb_q, ld_use_check_rs1_ans, ld_use_check_rs2_ans, MA_EX_rs2_ans, not_1_out,
       or_2_out, RW_EX_rs2_ans, RW_MA_rs2_ans, RW_OF_rs1_ans, RW_OF_rs2_ans;
  wire [1:0] and_2_out, isLD_3_q, RW_EX_rs1_ans;
  wire [3:0] instr_3_q_2, instr_3_q_3, instr_3_q_4, multiplexer_12_out, multiplexer_13_out,
       multiplexer_18_out, register_file_1_displayd_2, register_file_1_displayd_3,
       register_file_1_displayd_4, register_file_1_displayd_5, register_file_1_displayd_6,
       register_file_1_displayd_7;
  wire [4:0] instr_4_q_2, xnor_1_out;
  wire [11:0] register_file_1_displayd;
  wire [12:0] ALUSignals, ALUsignals_2_q, ALUsignals_3_q, ALUsignals_q, control_unit_1_alusignals;
  wire [21:0] control_unit_1_isret;
  wire [23:0] PC_q_2;
  wire [26:0] instr_4_q;
  wire [31:0] A_q, adder_1_out, adder_2_out, adder_3_out, alu_1_aluresult, aluResults_2_q, aluResults_q, B_q,
       bit_extender_1_out, branchT_q, calculate_immediate_1_immx, instr, instr_2, instr_2_q, instr_3_q,
       instr_q, ldResult_q, memory_unit_1_ldresult, multiplexer_1_out, multiplexer_2_out, multiplexer_5_out,
       multiplexer_7_out, multiplexer_8_out, multiplexer_9_out, multiplexer_10_out, multiplexer_11_out,
       multiplexer_14_out, multiplexer_15_out, multiplexer_16_out, multiplexer_17_out, op2_2_q, op2_q,
       pc_2_q, pc_3_q, pc_4_q, pc_5_q, PC_q, register_file_1_readd1, register_file_1_readd2, shifter_1_out,
       temp_instr, temp_instr_2;

  assign xnor_1_out = ~(instr_q[31:27] ^ 5'b01111);  // XNOR_Gate xnor_1, 5 bits wide
  and and_1 (and_1_out, xnor_1_out[0], xnor_1_out[1], xnor_1_out[2], xnor_1_out[3], xnor_1_out[4]);
  not not_1 (not_1_out, and_1_out);
  and and_2 (and_2_out[0], not_1_out, RW_EX_rs2_ans);
  and and_3 (and_2_out[1], not_1_out, MA_EX_rs2_ans);
  Datalock_Checker ld_use_check (
    .Earlier_Instruction(instr_q), .Later_Instruction({instr_4_q_2, instr_4_q}),
    .rs1_ans(ld_use_check_rs1_ans), .rs2_ans(ld_use_check_rs2_ans));
  or or_1 (IsldUse, ld_use_check_rs1_ans, ld_use_check_rs2_ans);
  Multiplexer #(.width(32)) multiplexer_1 (
    .in0(32'h4), .in1({32{1'b0}}), .out(multiplexer_1_out), .sel(IsldUse));  // open: en
  Forwarding_Conflict_Checker MA_EX (
    .Earlier_Instruction(instr_2_q), .Later_Instruction(instr_q), .rs1_ans(RW_EX_rs1_ans[1]),
    .rs2_ans(MA_EX_rs2_ans));
  Forwarding_Conflict_Checker RW_MA (
    .Earlier_Instruction({instr_3_q[31:26], instr_3_q_4, instr_3_q_3, instr_3_q_2, instr_3_q[13:0]}),
    .Later_Instruction(instr_2_q), .rs2_ans(RW_MA_rs2_ans));  // open: rs1_ans
  Forwarding_Conflict_Checker RW_OF (
    .Earlier_Instruction({instr_3_q[31:26], instr_3_q_4, instr_3_q_3, instr_3_q_2, instr_3_q[13:0]}),
    .Later_Instruction({instr_4_q_2, instr_4_q}), .rs1_ans(RW_OF_rs1_ans), .rs2_ans(RW_OF_rs2_ans));
  Forwarding_Conflict_Checker RW_EX (
    .Earlier_Instruction({instr_3_q[31:26], instr_3_q_4, instr_3_q_3, instr_3_q_2, instr_3_q[13:0]}),
    .Later_Instruction(instr_q), .rs1_ans(RW_EX_rs1_ans[0]), .rs2_ans(RW_EX_rs2_ans));
  Register #(.width(32), .trigger("falling")) PC (
    .D(multiplexer_2_out), .Q({PC_q[31:26], PC_q_2, PC_q[1:0]}), .clk(Clock), .clr(Reset));  // open: en
  Multiplexer #(.width(32), .enable("false")) multiplexer_2 (
    .in0(adder_1_out), .in1(multiplexer_5_out), .out(multiplexer_2_out), .sel(Branch));
  Multiplexer #(.width(32)) multiplexer_3 (
    .in0(temp_instr_2), .in1(32'h68000000), .out(instr_2), .sel(Branch));  // open: en
  Adder #(.width(32)) adder_1 (
    .a(multiplexer_1_out), .b({PC_q[31:26], PC_q_2, PC_q[1:0]}), .out(adder_1_out));  // open: cin, cout
  Register #(.width(32), .trigger("falling")) pc_2 (
    .D({PC_q[31:26], PC_q_2, PC_q[1:0]}), .Q(pc_2_q), .clk(Clock));  // open: en, clr
  Multiplexer #(.width(32)) multiplexer_4 (
    .in0(temp_instr), .in1(32'h68000000), .out(instr), .sel(Branch));  // open: en
  Register #(.width(32), .trigger("falling")) pc_3 (.D(pc_2_q), .Q(pc_3_q), .clk(Clock));  // open: en, clr
  Multiplexer #(.width(32), .enable("false")) multiplexer_5 (
    .in0(branchT_q), .in1(multiplexer_17_out), .out(multiplexer_5_out), .sel(isRet_q));
  Register #(.width(32), .trigger("falling")) pc_4 (.D(pc_3_q), .Q(pc_4_q), .clk(Clock));  // open: en, clr
  Register #(.width(32), .trigger("falling")) pc_5 (.D(pc_4_q), .Q(pc_5_q), .clk(Clock));  // open: en, clr
  assign bit_extender_1_out = {{5{instr_4_q[26]}}, instr_4_q};  // Bit_Extender bit_extender_1
  Multiplexer #(.width(32)) multiplexer_6 (
    .in0({instr_4_q_2, instr_4_q}), .in1(32'h68000000), .out(temp_instr), .sel(IsldUse));  // open: en
  Adder #(.width(32)) adder_2 (.a(pc_5_q), .b(32'h4), .out(adder_2_out));  // open: cin, cout
  ROM #(.addrWidth(24), .dataWidth(32)) rom_1 (.addr(PC_q_2), .data(temp_instr_2));  // open: sel
  Multiplexer #(.width(32)) multiplexer_7 (
    .in0(instr_2), .in1({instr_4_q_2, instr_4_q}), .out(multiplexer_7_out), .sel(IsldUse));  // open: en
  Shifter #(.width(32)) shifter_1 (.in(bit_extender_1_out), .\dist (5'b00010), .out(shifter_1_out));
  Register #(.width(32), .trigger("falling")) u_instr (.D(instr), .Q(instr_q), .clk(Clock));  // open: en, clr
  Register #(.width(32), .trigger("falling")) u_instr_2 (.D(instr_q), .Q(instr_2_q), .clk(Clock));  // open: en, clr
  Register #(.width(32), .trigger("falling")) instr_3 (
    .D(instr_2_q), .Q({instr_3_q[31:26], instr_3_q_4, instr_3_q_3, instr_3_q_2, instr_3_q[13:0]}), .clk(Clock));  // open: en, clr
  Multiplexer #(.select(2), .width(32), .enable("false")) multiplexer_8 (
    .in0(aluResults_2_q), .in1(ldResult_q), .in2(adder_2_out), .out(multiplexer_8_out), .sel(isLD_3_q));  // open: in3
  Register #(.width(32), .trigger("falling")) instr_4 (
    .D(multiplexer_7_out), .Q({instr_4_q_2, instr_4_q}), .clk(Clock));  // open: en, clr
  Calculate_Immediate calculate_immediate_1 (.imm(instr_4_q[17:0]), .immx(calculate_immediate_1_immx));
  Adder #(.width(32)) adder_3 (.a(shifter_1_out), .b(pc_2_q), .out(adder_3_out));  // open: cin, cout
  Register #(.width(32), .trigger("falling")) op2 (.D(multiplexer_16_out), .Q(op2_q), .clk(Clock));  // open: en, clr
  Register #(.width(32), .trigger("falling")) ldResult (
    .D(memory_unit_1_ldresult), .Q(ldResult_q), .clk(Clock));  // open: en, clr
  Hex_Digit_Display hex_digit_display_1 (.value(register_file_1_displayd_7));  // open: dp
  Hex_Digit_Display hex_digit_display_2 (.value(register_file_1_displayd_6));  // open: dp
  Multiplexer #(.width(32), .enable("false")) multiplexer_9 (
    .in0(multiplexer_14_out), .in1(calculate_immediate_1_immx), .out(multiplexer_9_out),
    .sel(control_unit_1_isret[15]));
  Register #(.width(32), .trigger("falling")) branchT (.D(adder_3_out), .Q(branchT_q), .clk(Clock));  // open: en, clr
  ALU alu_1 (
    .A(multiplexer_17_out), .B(multiplexer_11_out), .ALUsignals(ALUsignals_q), .aluResult(alu_1_aluresult),
    .is(alu_1_is), .is_2(alu_1_is_2));
  Multiplexer #(.width(32), .enable("false")) multiplexer_10 (
    .in0(op2_q), .in1(multiplexer_8_out), .out(multiplexer_10_out), .sel(RW_MA_rs2_ans));
  Memory_Unit memory_unit_1 (
    .MAR(aluResults_q), .ldResult(memory_unit_1_ldresult), .MDR(multiplexer_10_out), .isSt(isSt_2_q),
    .isLd(isLD_2_q), .Clock(Clock), .Reset(Reset));
  Hex_Digit_Display hex_digit_display_3 (.value(register_file_1_displayd_5));  // open: dp
  Clock u_Clock (.out(Clock));
  Register #(.width(32), .trigger("falling")) B (.D(multiplexer_9_out), .Q(B_q), .clk(Clock));  // open: en, clr
  Multiplexer #(.select(2), .width(32), .enable("false")) multiplexer_11 (
    .in0(B_q), .in1(multiplexer_8_out), .in2(aluResults_q), .in3(aluResults_q), .out(multiplexer_11_out),
    .sel(and_2_out));
  Hex_Digit_Display hex_digit_display_4 (.value(register_file_1_displayd_4));  // open: dp
  Register #(.width(32), .trigger("falling")) op2_2 (
    .D(multiplexer_14_out), .Q(op2_2_q), .clk(Clock));  // open: en, clr
  Flags flags_1 (
    .isCmp(ALUsignals_q[0]), .is(alu_1_is), .is_2(alu_1_is_2), .flags_GT(flags_1_flags_gt),
    .flags_E(flags_1_flags_e));
  Hex_Digit_Display hex_digit_display_5 (.value(register_file_1_displayd_3));  // open: dp
  Hex_Digit_Display hex_digit_display_6 (.value(register_file_1_displayd[11:8]));  // open: dp
  Multiplexer #(.width(4), .enable("false")) multiplexer_12 (
    .in0(instr_4_q[21:18]), .in1(4'b1111), .out(multiplexer_12_out), .sel(control_unit_1_isret[0]));
  Multiplexer #(.width(4), .enable("false")) multiplexer_13 (
    .in0(instr_4_q[17:14]), .in1(instr_4_q[25:22]), .out(multiplexer_13_out), .sel(control_unit_1_isret[17]));
  Multiplexer #(.width(32), .enable("false")) multiplexer_14 (
    .in0(register_file_1_readd2), .in1(multiplexer_8_out), .out(multiplexer_14_out), .sel(RW_OF_rs2_ans));
  Multiplexer #(.width(32), .enable("false")) multiplexer_15 (
    .in0(register_file_1_readd1), .in1(multiplexer_8_out), .out(multiplexer_15_out), .sel(RW_OF_rs1_ans));
  Multiplexer #(.width(32), .enable("false")) multiplexer_16 (
    .in0(op2_2_q), .in1(multiplexer_8_out), .out(multiplexer_16_out), .sel(RW_EX_rs2_ans));
  Register #(.width(32), .trigger("falling")) aluResults (
    .D(alu_1_aluresult), .Q(aluResults_q), .clk(Clock));  // open: en, clr
  Register #(.width(32), .trigger("falling")) aluResults_2 (
    .D(aluResults_q), .Q(aluResults_2_q), .clk(Clock));  // open: en, clr
  Hex_Digit_Display hex_digit_display_7 (.value(register_file_1_displayd_2));  // open: dp
  Register_File register_file_1 (
    .ReadA1(multiplexer_12_out), .ReadA2(multiplexer_13_out), .WriteE(isWb_3_q), .WriteD(multiplexer_8_out),
    .ReadD1(register_file_1_readd1), .ReadD2(register_file_1_readd2), .Clock(Clock), .Reset(Reset),
    .DisplayD({register_file_1_displayd_7, register_file_1_displayd_6, register_file_1_displayd_5, register_file_1_displayd_4, register_file_1_displayd_3, register_file_1_displayd[11:8], register_file_1_displayd_2, register_file_1_displayd[3:0]}),
    .DisplayA(Display_Address), .WriteA(multiplexer_18_out));
  Register #(.width(32), .trigger("falling")) A (.D(multiplexer_15_out), .Q(A_q), .clk(Clock));  // open: en, clr
  Multiplexer #(.select(2), .width(32), .enable("false")) multiplexer_17 (
    .in0(A_q), .in1(multiplexer_8_out), .in2(aluResults_q), .in3(aluResults_q), .out(multiplexer_17_out),
    .sel(RW_EX_rs1_ans));
  Branch_Unit branch_unit_1 (
    .isBeq(isBeq_q), .isUBranch(isUBranch_q), .flags_E(flags_1_flags_e), .isBgt(isBgt_q),
    .flags_GT(flags_1_flags_gt), .isBranchTaken(Branch));
  Multiplexer #(.width(4), .enable("false")) multiplexer_18 (
    .in0(instr_3_q_4), .in1(4'b1111), .out(multiplexer_18_out), .sel(isLD_3_q[1]));
  Hex_Digit_Display hex_digit_display_8 (.value(register_file_1_displayd[3:0]));  // open: dp
  Register #(.width(1), .trigger("falling")) u_isRet (.D(IsRet), .Q(isRet_q), .clk(Clock));  // open: en, clr
  Register #(.width(1), .trigger("falling")) u_isImmediate (
    .D(isImmediate), .Q(isImmediate_q), .clk(Clock));  // open: en, clr
  Register #(.width(1), .trigger("falling")) isRet_2 (.D(isRet_q), .Q(isRet_2_q), .clk(Clock));  // open: en, clr
  Register #(.width(1), .trigger("falling")) isImmediate_2 (
    .D(isImmediate_q), .Q(isImmediate_2_q), .clk(Clock));  // open: en, clr
  Register #(.width(1), .trigger("falling")) isRet_3 (.D(isRet_2_q), .Q(isRet_3_q), .clk(Clock));  // open: en, clr
  Register #(.width(1), .trigger("falling")) isImmediate_3 (.D(isImmediate_2_q), .clk(Clock));  // open: en, Q, clr
  Control_Unit control_unit_1 (
    .isSt(control_unit_1_isret[17]), .isLd(control_unit_1_isret[16]), .isBeq(control_unit_1_isret[19]),
    .isBgt(control_unit_1_isret[20]), .isRet(control_unit_1_isret[0]), .I_bit(instr_4_q[26]),
    .isImmediate(control_unit_1_isret[15]), .opcode(instr_4_q_2), .isWb(control_unit_1_isret[1]),
    .isUbranch(control_unit_1_isret[21]), .isCall(control_unit_1_isret[18]),
    .ALUsignals(control_unit_1_alusignals));
  Register #(.width(1), .trigger("falling")) u_isSt (.D(isSt), .Q(isSt_q), .clk(Clock));  // open: en, clr
  Register #(.width(1), .trigger("falling")) isSt_2 (.D(isSt_q), .Q(isSt_2_q), .clk(Clock));  // open: en, clr
  Register #(.width(1), .trigger("falling")) isSt_3 (.D(isSt_2_q), .Q(isSt_3_q), .clk(Clock));  // open: en, clr
  Register #(.width(1), .trigger("falling")) u_isWb (.D(IsWb), .Q(isWb_q), .clk(Clock));  // open: en, clr
  Register #(.width(1), .trigger("falling")) isWb_2 (.D(isWb_q), .Q(isWb_2_q), .clk(Clock));  // open: en, clr
  Register #(.width(1), .trigger("falling")) isWb_3 (.D(isWb_2_q), .Q(isWb_3_q), .clk(Clock));  // open: en, clr
  Register #(.width(1), .trigger("falling")) u_isLD (.D(isLd), .Q(isLD_q), .clk(Clock));  // open: en, clr
  Register #(.width(13), .trigger("falling")) u_ALUsignals (
    .D(ALUSignals), .Q(ALUsignals_q), .clk(Clock));  // open: en, clr
  Register #(.width(1), .trigger("falling")) isLD_2 (.D(isLD_q), .Q(isLD_2_q), .clk(Clock));  // open: en, clr
  Register #(.width(13), .trigger("falling")) ALUsignals_2 (
    .D(ALUsignals_q), .Q(ALUsignals_2_q), .clk(Clock));  // open: en, clr
  Register #(.width(1), .trigger("falling")) isLD_3 (.D(isLD_2_q), .Q(isLD_3_q[0]), .clk(Clock));  // open: en, clr
  Register #(.width(13), .trigger("falling")) ALUsignals_3 (
    .D(ALUsignals_2_q), .Q(ALUsignals_3_q), .clk(Clock));  // open: en, clr
  Register #(.width(1), .trigger("falling")) u_isCall (.D(isCall), .Q(isCall_q), .clk(Clock));  // open: en, clr
  Register #(.width(1), .trigger("falling")) isCall_2 (.D(isCall_q), .Q(isCall_2_q), .clk(Clock));  // open: en, clr
  Register #(.width(1), .trigger("falling")) isCall_3 (.D(isCall_2_q), .Q(isLD_3_q[1]), .clk(Clock));  // open: en, clr
  Register #(.width(1), .trigger("falling")) u_isBeq (.D(isBeq), .Q(isBeq_q), .clk(Clock));  // open: en, clr
  Register #(.width(1), .trigger("falling")) isBeq_2 (.D(isBeq_q), .Q(isBeq_2_q), .clk(Clock));  // open: en, clr
  Register #(.width(1), .trigger("falling")) isBeq_3 (.D(isBeq_2_q), .Q(isBeq_3_q), .clk(Clock));  // open: en, clr
  Register #(.width(1), .trigger("falling")) u_isUBranch (
    .D(isUBranch), .Q(isUBranch_q), .clk(Clock));  // open: en, clr
  Register #(.width(1), .trigger("falling")) u_isBgt (.D(isBgt), .Q(isBgt_q), .clk(Clock));  // open: en, clr
  Register #(.width(1), .trigger("falling")) isBgt_2 (.D(isBgt_q), .Q(isBgt_2_q), .clk(Clock));  // open: en, clr
  Register #(.width(1), .trigger("falling")) isUBranch_2 (
    .D(isUBranch_q), .Q(isUBranch_2_q), .clk(Clock));  // open: en, clr
  Register #(.width(1), .trigger("falling")) isBgt_3 (.D(isBgt_2_q), .Q(isBgt_3_q), .clk(Clock));  // open: en, clr
  Register #(.width(1), .trigger("falling")) isUBranch_3 (
    .D(isUBranch_2_q), .Q(isUBranch_3_q), .clk(Clock));  // open: en, clr
  Multiplexer #(.width(22)) multiplexer_19 (
    .in0({control_unit_1_isret[21:15], control_unit_1_alusignals, control_unit_1_isret[1:0]}),
    .in1({22{1'b0}}),
    .out({isUBranch, isBgt, isBeq, isCall, isSt, isLd, isImmediate, ALUSignals, IsWb, IsRet}), .sel(or_2_out));  // open: en
  or or_2 (or_2_out, Branch, IsldUse);

  // Notes on the sheet:
  //   isBranchTaken
  //   IF-OF
  //   OF-EX
  //   isBranchTaken
  //   branchPC
  //   EX-MA
  //   MA-RW
  //   pc+4
  //   branchTarget
  //   aluresult ma
  //   pc
  //   pc
  //   imm
  //   offset
  //   isCall
  //   immx
  //   calc immx
  //   ALU
  //   aluResult
  //   is>
  //   is=
  //   flags(E)
  //   Display Register
  //   rs1
  //   rd
  //   isSt
  //   flags(GT)
  //   isRet
  //   Branch
  //   isCall
  //   rd
  //   opcode
  //   I bit
  //   CONTROL
  //   isBeq
  //   isBgt
  //   isUBranch
  //   Data rw
endmodule

module Control_Unit (
  input  I_bit,
  input  [4:0] opcode,
  output isSt,
  output isLd,
  output isBeq,
  output isBgt,
  output isRet,
  output isImmediate,
  output isWb,
  output isUbranch,
  output isCall,
  output [12:0] ALUsignals
);

  wire and_6_out, and_7_out, and_8_out, and_9_out, and_10_out, and_12_out, and_13_out, nand_1_out;

  nand nand_1 (nand_1_out, opcode[0], opcode[1]);
  and and_1 (isSt, opcode[0], opcode[1], opcode[2], opcode[3], ~opcode[4]);  // AND_Gate
  and and_2 (isLd, ~opcode[0], opcode[1], opcode[2], opcode[3], ~opcode[4]);  // AND_Gate
  and and_3 (isBeq, ~opcode[0], ~opcode[1], ~opcode[2], ~opcode[3], opcode[4]);  // AND_Gate
  and and_4 (isBgt, opcode[0], ~opcode[1], ~opcode[2], ~opcode[3], opcode[4]);  // AND_Gate
  and and_5 (isRet, ~opcode[0], ~opcode[1], opcode[2], ~opcode[3], opcode[4]);  // AND_Gate
  and and_6 (and_6_out, opcode[0], ~opcode[1], opcode[2], ~opcode[4]);  // AND_Gate
  and and_7 (and_7_out, opcode[0], opcode[2], opcode[3], ~opcode[4]);  // AND_Gate
  and and_8 (and_8_out, opcode[4], nand_1_out);
  and and_9 (and_9_out, opcode[1], ~opcode[2], ~opcode[3], opcode[4]);  // AND_Gate
  and and_10 (and_10_out, ~opcode[0], ~opcode[1], opcode[2], ~opcode[3], opcode[4]);  // AND_Gate
  and and_11 (isCall, opcode[0], opcode[1], ~opcode[2], ~opcode[3], opcode[4]);  // AND_Gate
  and and_12 (and_12_out, ~opcode[0], ~opcode[1], ~opcode[2], ~opcode[3], ~opcode[4]);  // AND_Gate
  and and_13 (and_13_out, opcode[1], opcode[2], opcode[3], ~opcode[4]);  // AND_Gate
  and isSub (ALUsignals[2], opcode[0], ~opcode[1], ~opcode[2], ~opcode[3], ~opcode[4]);  // AND_Gate
  and isCmp (ALUsignals[0], opcode[0], ~opcode[1], opcode[2], ~opcode[3], ~opcode[4]);  // AND_Gate
  and isMul (ALUsignals[3], ~opcode[0], opcode[1], ~opcode[2], ~opcode[3], ~opcode[4]);  // AND_Gate
  and isDiv (ALUsignals[4], opcode[0], opcode[1], ~opcode[2], ~opcode[3], ~opcode[4]);  // AND_Gate
  and isMod (ALUsignals[5], ~opcode[0], ~opcode[1], opcode[2], ~opcode[3], ~opcode[4]);  // AND_Gate
  and isLsl (ALUsignals[7], ~opcode[0], opcode[1], ~opcode[2], opcode[3], ~opcode[4]);  // AND_Gate
  and isLsr (ALUsignals[8], opcode[0], opcode[1], ~opcode[2], opcode[3], ~opcode[4]);  // AND_Gate
  and isAsr (ALUsignals[9], ~opcode[0], ~opcode[1], opcode[2], opcode[3], ~opcode[4]);  // AND_Gate
  and isOr (ALUsignals[12], opcode[0], opcode[1], opcode[2], ~opcode[3], ~opcode[4]);  // AND_Gate
  and isAnd (ALUsignals[11], ~opcode[0], opcode[1], opcode[2], ~opcode[3], ~opcode[4]);  // AND_Gate
  and isNot (ALUsignals[10], ~opcode[0], ~opcode[1], ~opcode[2], opcode[3], ~opcode[4]);  // AND_Gate
  and isMov (ALUsignals[6], opcode[0], ~opcode[1], ~opcode[2], opcode[3], ~opcode[4]);  // AND_Gate
  or or_1 (isUbranch, and_9_out, and_10_out);
  or isAdd (ALUsignals[1], and_12_out, and_13_out);
  nor nor_1 (isWb, and_6_out, and_7_out, and_8_out);

  assign isImmediate = I_bit;

  // Notes on the sheet:
  //   op1
  //   op2
  //   op3
  //   op4
  //   op5
endmodule

module Register_File (
  input  Clock,
  input  Reset,
  input  [31:0] WriteD,
  input  [3:0] ReadA1,
  input  WriteE,
  input  [3:0] WriteA,
  input  [3:0] ReadA2,
  input  [3:0] DisplayA,
  output [31:0] ReadD1,
  output [31:0] ReadD2,
  output [31:0] DisplayD
);

  wire demultiplexer_1_out0, demultiplexer_1_out1, demultiplexer_1_out2, demultiplexer_1_out3,
       demultiplexer_1_out4, demultiplexer_1_out5, demultiplexer_1_out6, demultiplexer_1_out7,
       demultiplexer_1_out8, demultiplexer_1_out9, demultiplexer_1_out10, demultiplexer_1_out11,
       demultiplexer_1_out12, demultiplexer_1_out13, demultiplexer_1_out14, demultiplexer_1_out15,
       multiplexer_2_out, or_1_out, or_2_out;
  wire [31:0] multiplexer_1_out, r0_q, r1_q, r2_q, r3_q, r4_q, r5_q, r6_q, r7_q, r8_q, r9_q, r10_q, r11_q,
       r12_q, r13_q, r14_q, r15_q;

  Demultiplexer #(.select(4), .disabled(0), .enable("false")) demultiplexer_1 (
    .out0(demultiplexer_1_out0), .out1(demultiplexer_1_out1), .out2(demultiplexer_1_out2),
    .out3(demultiplexer_1_out3), .out4(demultiplexer_1_out4), .out5(demultiplexer_1_out5),
    .out6(demultiplexer_1_out6), .out7(demultiplexer_1_out7), .out8(demultiplexer_1_out8),
    .out9(demultiplexer_1_out9), .out10(demultiplexer_1_out10), .out11(demultiplexer_1_out11),
    .out12(demultiplexer_1_out12), .out13(demultiplexer_1_out13), .out14(demultiplexer_1_out14),
    .out15(demultiplexer_1_out15), .in(WriteE), .sel(WriteA));
  Multiplexer #(.width(32), .enable("false")) multiplexer_1 (
    .in0(WriteD), .in1(32'h3fffffc), .out(multiplexer_1_out), .sel(Reset));
  or or_1 (or_1_out, demultiplexer_1_out14, Reset);
  Multiplexer #(.enable("false")) multiplexer_2 (.in0(or_2_out), .out(multiplexer_2_out), .sel(1'b0));  // open: in1
  or or_2 (or_2_out, Clock, Reset);
  Register #(.width(32)) r0 (.D(WriteD), .en(demultiplexer_1_out0), .Q(r0_q), .clk(Clock), .clr(Reset));
  Register #(.width(32)) r1 (.D(WriteD), .en(demultiplexer_1_out1), .Q(r1_q), .clk(Clock), .clr(Reset));
  Register #(.width(32)) r2 (.D(WriteD), .en(demultiplexer_1_out2), .Q(r2_q), .clk(Clock), .clr(Reset));
  Register #(.width(32)) r3 (.D(WriteD), .en(demultiplexer_1_out3), .Q(r3_q), .clk(Clock), .clr(Reset));
  Register #(.width(32)) r4 (.D(WriteD), .en(demultiplexer_1_out4), .Q(r4_q), .clk(Clock), .clr(Reset));
  Register #(.width(32)) r5 (.D(WriteD), .en(demultiplexer_1_out5), .Q(r5_q), .clk(Clock), .clr(Reset));
  Register #(.width(32)) r6 (.D(WriteD), .en(demultiplexer_1_out6), .Q(r6_q), .clk(Clock), .clr(Reset));
  Register #(.width(32)) r7 (.D(WriteD), .en(demultiplexer_1_out7), .Q(r7_q), .clk(Clock), .clr(Reset));
  Register #(.width(32)) r8 (.D(WriteD), .en(demultiplexer_1_out8), .Q(r8_q), .clk(Clock), .clr(Reset));
  Register #(.width(32)) r9 (.D(WriteD), .en(demultiplexer_1_out9), .Q(r9_q), .clk(Clock), .clr(Reset));
  Register #(.width(32)) r10 (.D(WriteD), .en(demultiplexer_1_out10), .Q(r10_q), .clk(Clock), .clr(Reset));
  Register #(.width(32)) r11 (.D(WriteD), .en(demultiplexer_1_out11), .Q(r11_q), .clk(Clock), .clr(Reset));
  Register #(.width(32)) r12 (.D(WriteD), .en(demultiplexer_1_out12), .Q(r12_q), .clk(Clock), .clr(Reset));
  Register #(.width(32)) r13 (.D(WriteD), .en(demultiplexer_1_out13), .Q(r13_q), .clk(Clock), .clr(Reset));
  Register #(.width(32)) r14 (.D(multiplexer_1_out), .en(or_1_out), .Q(r14_q), .clk(multiplexer_2_out));  // open: clr
  Register #(.width(32)) r15 (.D(WriteD), .en(demultiplexer_1_out15), .Q(r15_q), .clk(Clock), .clr(Reset));
  Multiplexer #(.select(4), .width(32), .disabled(0), .enable("false")) multiplexer_3 (
    .in0(r0_q), .in1(r1_q), .in2(r2_q), .in3(r3_q), .in4(r4_q), .in5(r5_q), .in6(r6_q), .in7(r7_q),
    .in8(r8_q), .in9(r9_q), .in10(r10_q), .in11(r11_q), .in12(r12_q), .in13(r13_q), .in14(r14_q),
    .in15(r15_q), .out(ReadD1), .sel(ReadA1));
  Multiplexer #(.select(4), .width(32), .disabled(0), .enable("false")) multiplexer_4 (
    .in0(r0_q), .in1(r1_q), .in2(r2_q), .in3(r3_q), .in4(r4_q), .in5(r5_q), .in6(r6_q), .in7(r7_q),
    .in8(r8_q), .in9(r9_q), .in10(r10_q), .in11(r11_q), .in12(r12_q), .in13(r13_q), .in14(r14_q),
    .in15(r15_q), .out(ReadD2), .sel(ReadA2));
  Multiplexer #(.select(4), .width(32), .disabled(0), .enable("false")) multiplexer_5 (
    .in0(r0_q), .in1(r1_q), .in2(r2_q), .in3(r3_q), .in4(r4_q), .in5(r5_q), .in6(r6_q), .in7(r7_q),
    .in8(r8_q), .in9(r9_q), .in10(r10_q), .in11(r11_q), .in12(r12_q), .in13(r13_q), .in14(r14_q),
    .in15(r15_q), .out(DisplayD), .sel(DisplayA));
endmodule

module ALU (
  input  [31:0] A,
  input  [31:0] B,
  input  [12:0] ALUsignals,
  output [31:0] aluResult,
  output is,
  output is_2
);

  wire [31:0] adder_1_out, and_1_out, divider_1_out, divider_1_rem, multiplier_1_out, not_1_out, or_1_out,
       shifter_1_out, shifter_2_out, shifter_3_out, subtractor_1_out;

  Adder #(.width(32)) adder_1 (.a(A), .b(B), .out(adder_1_out));  // open: cin, cout
  Subtractor #(.width(32)) subtractor_1 (.a(A), .b(B), .out(subtractor_1_out));  // open: bin, bout
  Multiplier #(.width(32)) multiplier_1 (.a(A), .b(B), .out(multiplier_1_out));  // open: cin, cout
  Divider #(.width(32)) divider_1 (.a(A), .b(B), .out(divider_1_out), .rem(divider_1_rem));  // open: upper
  Comparator #(.width(32)) comparator_1 (.a(A), .b(B), .gt(is), .eq(is_2));  // open: lt
  Shifter #(.width(32)) shifter_1 (.in(A), .\dist (B[4:0]), .out(shifter_1_out));
  Shifter #(.width(32), .shift("lr")) shifter_2 (.in(A), .\dist (B[4:0]), .out(shifter_2_out));
  Shifter #(.width(32), .shift("ar")) shifter_3 (.in(A), .\dist (B[4:0]), .out(shifter_3_out));
  assign not_1_out = ~B;  // NOT_Gate not_1, 32 bits wide
  assign and_1_out = A & B;  // AND_Gate and_1, 32 bits wide
  assign or_1_out = A | B;  // OR_Gate or_1, 32 bits wide
  assign aluResult = ALUsignals[1] ? adder_1_out : 32'bz;  // Controlled_Buffer controlled_buffer_1
  assign aluResult = ALUsignals[2] ? subtractor_1_out : 32'bz;  // Controlled_Buffer controlled_buffer_2
  assign aluResult = ALUsignals[3] ? multiplier_1_out : 32'bz;  // Controlled_Buffer controlled_buffer_3
  assign aluResult = ALUsignals[4] ? divider_1_out : 32'bz;  // Controlled_Buffer controlled_buffer_4
  assign aluResult = ALUsignals[5] ? divider_1_rem : 32'bz;  // Controlled_Buffer controlled_buffer_5
  assign aluResult = ALUsignals[6] ? B : 32'bz;  // Controlled_Buffer controlled_buffer_6
  assign aluResult = ALUsignals[7] ? shifter_1_out : 32'bz;  // Controlled_Buffer controlled_buffer_7
  assign aluResult = ALUsignals[8] ? shifter_2_out : 32'bz;  // Controlled_Buffer controlled_buffer_8
  assign aluResult = ALUsignals[9] ? shifter_3_out : 32'bz;  // Controlled_Buffer controlled_buffer_9
  assign aluResult = ALUsignals[10] ? not_1_out : 32'bz;  // Controlled_Buffer controlled_buffer_10
  assign aluResult = ALUsignals[11] ? and_1_out : 32'bz;  // Controlled_Buffer controlled_buffer_11
  assign aluResult = ALUsignals[12] ? or_1_out : 32'bz;  // Controlled_Buffer controlled_buffer_12

  // Notes on the sheet:
  //   add
  //   sub
  //   mul
  //   div
  //   cmp
  //   lsr
  //   mod
  //   lsl
  //   asr
endmodule

module Flags (
  input  isCmp,
  input  is,
  input  is_2,
  output flags_GT,
  output flags_E
);

  D_Flip_Flop #(.trigger("high")) d_ff_1 (.clk(isCmp), .D(is), .Q(flags_GT));  // open: Qn, preset, en, reset
  D_Flip_Flop #(.trigger("high")) d_ff_2 (.clk(isCmp), .D(is_2), .Q(flags_E));  // open: Qn, preset, en, reset
endmodule

module Branch_Unit (
  input  isUBranch,
  input  isBeq,
  input  flags_E,
  input  isBgt,
  input  flags_GT,
  output isBranchTaken
);

  wire and_1_out, and_2_out;

  and and_1 (and_1_out, isBeq, flags_E);
  and and_2 (and_2_out, isBgt, flags_GT);
  or or_1 (isBranchTaken, isUBranch, and_1_out, and_2_out);
endmodule

module Memory_Unit (
  input  [31:0] MAR,
  input  isLd,
  input  [31:0] MDR,
  input  isSt,
  input  Clock,
  input  Reset,
  output [31:0] ldResult
);

  RAM #(.addrWidth(24), .dataWidth(32), .bus("separate")) ram_1 (
    .addr(MAR[25:2]), .din(MDR), .data(ldResult), .str(isSt), .clk(Clock), .ld(isLd), .clr(Reset));  // open: sel
endmodule

module Calculate_Immediate (
  input  [17:0] imm,
  output [31:0] immx
);

  wire [31:0] bit_extender_1_out, bit_extender_2_out, shifter_1_out;

  assign bit_extender_1_out = {{16{1'b0}}, imm[15:0]};  // Bit_Extender bit_extender_1
  assign bit_extender_2_out = {{16{imm[15]}}, imm[15:0]};  // Bit_Extender bit_extender_2
  Shifter #(.width(32)) shifter_1 (.in(bit_extender_1_out), .\dist (5'b10000), .out(shifter_1_out));
  Multiplexer #(.select(2), .width(32), .enable("false")) multiplexer_1 (
    .in0(bit_extender_2_out), .in1(bit_extender_1_out), .in2(shifter_1_out), .out(immx), .sel(imm[17:16]));  // open: in3

  // Notes on the sheet:
  //   modifier bits
  //   high
  //   default
  //   unsigned
endmodule

module Forwarding_Conflict_Checker (
  input  [31:0] Earlier_Instruction,
  input  [31:0] Later_Instruction,
  output rs1_ans,
  output rs2_ans
);

  wire and_1_out, and_3_out, and_4_out, b_2_out, b_out, beq_2_out, beq_out, bgt_2_out, bgt_out, call_2_out,
       call_out, cmp_out, mov_out, nand_1_out, nop_2_out, nop_out, nor_1_out, nor_2_out, not_2_out, not_out,
       or_1_out, ret_2_out, ret_out, st_out;
  wire [3:0] multiplexer_1_out, multiplexer_2_out, multiplexer_3_out, xnor_1_out, xnor_2_out;
  wire [4:0] xor_1_out;

  Multiplexer #(.width(4)) multiplexer_1 (
    .in0(Later_Instruction[17:14]), .in1(Later_Instruction[25:22]), .out(multiplexer_1_out), .sel(not_2_out));  // open: en
  and call (call_out, Earlier_Instruction[31], ~Earlier_Instruction[30], ~Earlier_Instruction[29], Earlier_Instruction[28], Earlier_Instruction[27]);  // AND_Gate
  and nop (nop_out, ~Earlier_Instruction[31], Earlier_Instruction[30], Earlier_Instruction[29], ~Earlier_Instruction[28], Earlier_Instruction[27]);  // AND_Gate
  and cmp (cmp_out, ~Earlier_Instruction[31], ~Earlier_Instruction[30], Earlier_Instruction[29], ~Earlier_Instruction[28], Earlier_Instruction[27]);  // AND_Gate
  and st (st_out, ~Earlier_Instruction[31], Earlier_Instruction[30], Earlier_Instruction[29], Earlier_Instruction[28], Earlier_Instruction[27]);  // AND_Gate
  and b (b_out, Earlier_Instruction[31], ~Earlier_Instruction[30], ~Earlier_Instruction[29], Earlier_Instruction[28], ~Earlier_Instruction[27]);  // AND_Gate
  and nop_2 (nop_2_out, ~Later_Instruction[31], Later_Instruction[30], Later_Instruction[29], ~Later_Instruction[28], Later_Instruction[27]);  // AND_Gate
  and \not  (not_out, ~Later_Instruction[31], Later_Instruction[30], ~Later_Instruction[29], ~Later_Instruction[28], ~Later_Instruction[27]);  // AND_Gate
  and mov (mov_out, ~Later_Instruction[31], Later_Instruction[30], ~Later_Instruction[29], ~Later_Instruction[28], Later_Instruction[27]);  // AND_Gate
  and b_2 (b_2_out, Later_Instruction[31], ~Later_Instruction[30], ~Later_Instruction[29], Later_Instruction[28], ~Later_Instruction[27]);  // AND_Gate
  not not_2 (not_2_out, or_1_out);
  and beq (beq_out, Earlier_Instruction[31], ~Earlier_Instruction[30], ~Earlier_Instruction[29], ~Earlier_Instruction[28], ~Earlier_Instruction[27]);  // AND_Gate
  and bgt (bgt_out, Earlier_Instruction[31], ~Earlier_Instruction[30], ~Earlier_Instruction[29], ~Earlier_Instruction[28], Earlier_Instruction[27]);  // AND_Gate
  and ret (ret_out, Earlier_Instruction[31], ~Earlier_Instruction[30], Earlier_Instruction[29], ~Earlier_Instruction[28], ~Earlier_Instruction[27]);  // AND_Gate
  and beq_2 (beq_2_out, Later_Instruction[31], ~Later_Instruction[30], ~Later_Instruction[29], ~Later_Instruction[28], ~Later_Instruction[27]);  // AND_Gate
  and bgt_2 (bgt_2_out, Later_Instruction[31], ~Later_Instruction[30], ~Later_Instruction[29], ~Later_Instruction[28], Later_Instruction[27]);  // AND_Gate
  and ret_2 (ret_2_out, Later_Instruction[31], ~Later_Instruction[30], Later_Instruction[29], ~Later_Instruction[28], ~Later_Instruction[27]);  // AND_Gate
  and call_2 (call_2_out, Later_Instruction[31], ~Later_Instruction[30], ~Later_Instruction[29], Later_Instruction[28], Later_Instruction[27]);  // AND_Gate
  nor nor_1 (nor_1_out, nop_out, cmp_out, st_out, b_out, beq_out, bgt_out, ret_out, nop_2_out, not_out, mov_out, b_2_out, beq_2_out, bgt_2_out, call_2_out);
  Multiplexer #(.width(4)) multiplexer_2 (
    .in0(Earlier_Instruction[25:22]), .in1(4'b1111), .out(multiplexer_2_out), .sel(call_out));  // open: en
  Multiplexer #(.width(4)) multiplexer_3 (
    .in0(Later_Instruction[21:18]), .in1(4'b1111), .out(multiplexer_3_out), .sel(ret_2_out));  // open: en
  assign xnor_1_out = ~(multiplexer_2_out ^ multiplexer_3_out);  // XNOR_Gate xnor_1, 4 bits wide
  and and_1 (and_1_out, xnor_1_out[0], xnor_1_out[1], xnor_1_out[2], xnor_1_out[3]);
  assign xnor_2_out = ~(multiplexer_1_out ^ multiplexer_2_out);  // XNOR_Gate xnor_2, 4 bits wide
  and and_2 (rs1_ans, nor_1_out, and_1_out);
  and and_3 (and_3_out, xnor_2_out[0], xnor_2_out[1], xnor_2_out[2], xnor_2_out[3]);
  assign xor_1_out = 5'b01111 ^ Later_Instruction[31:27];  // XOR_Gate xor_1, 5 bits wide
  and and_4 (and_4_out, Later_Instruction[26], 1'b1);
  nor nor_2 (nor_2_out, nop_out, st_out, cmp_out, ret_out, b_out, beq_out, bgt_out, b_2_out, nop_2_out, beq_2_out, bgt_2_out, call_2_out);
  or or_1 (or_1_out, xor_1_out[0], xor_1_out[1], xor_1_out[2], xor_1_out[3], xor_1_out[4]);
  nand nand_1 (nand_1_out, or_1_out, and_4_out);
  and and_5 (rs2_ans, nor_2_out, nand_1_out, and_3_out);

  // Notes on the sheet:
  //   B
  //   A
  //   rd
  //   rs2
  //   opcode
  //   rs1
  //   rd
  //   opcode
  //   I
  //   I
  //   src2
  //   dest
  //   src1
  //   dest
endmodule

module Datalock_Checker (
  input  [31:0] Earlier_Instruction,
  input  [31:0] Later_Instruction,
  output rs1_ans,
  output rs2_ans
);

  wire and_1_out, and_2_out, and_3_out, b_out, beq_out, bgt_out, call_out, mov_out, nop_out, nor_1_out,
       not_2_out, not_3_out, not_4_out, not_out, or_1_out, ret_out, st_out;
  wire [3:0] multiplexer_1_out, multiplexer_2_out, multiplexer_3_out, xnor_1_out, xnor_2_out;

  and and_1 (and_1_out, Earlier_Instruction[27], ~Earlier_Instruction[28], ~Earlier_Instruction[29], Earlier_Instruction[30], Earlier_Instruction[31]);  // AND_Gate
  Multiplexer #(.width(4)) multiplexer_1 (
    .in0(Later_Instruction[17:14]), .in1(Later_Instruction[25:22]), .out(multiplexer_1_out), .sel(st_out));  // open: en
  and and_2 (and_2_out, ~Earlier_Instruction[27], Earlier_Instruction[28], Earlier_Instruction[29], Earlier_Instruction[30], ~Earlier_Instruction[31]);  // AND_Gate
  Multiplexer #(.width(4)) multiplexer_2 (
    .in0(Earlier_Instruction[25:22]), .in1(4'b1111), .out(multiplexer_2_out), .sel(and_1_out));  // open: en
  and mov (mov_out, ~Later_Instruction[31], Later_Instruction[30], ~Later_Instruction[29], ~Later_Instruction[28], Later_Instruction[27]);  // AND_Gate
  and \not  (not_out, ~Later_Instruction[31], Later_Instruction[30], ~Later_Instruction[29], ~Later_Instruction[28], ~Later_Instruction[27]);  // AND_Gate
  and ret (ret_out, Later_Instruction[31], ~Later_Instruction[30], Later_Instruction[29], ~Later_Instruction[28], ~Later_Instruction[27]);  // AND_Gate
  and st (st_out, ~Later_Instruction[31], Later_Instruction[30], Later_Instruction[29], Later_Instruction[28], Later_Instruction[27]);  // AND_Gate
  and call (call_out, Later_Instruction[31], ~Later_Instruction[30], ~Later_Instruction[29], Later_Instruction[28], Later_Instruction[27]);  // AND_Gate
  and nop (nop_out, ~Later_Instruction[31], Later_Instruction[30], Later_Instruction[29], ~Later_Instruction[28], Later_Instruction[27]);  // AND_Gate
  and bgt (bgt_out, Later_Instruction[31], ~Later_Instruction[30], ~Later_Instruction[29], ~Later_Instruction[28], Later_Instruction[27]);  // AND_Gate
  and beq (beq_out, Later_Instruction[31], ~Later_Instruction[30], ~Later_Instruction[29], ~Later_Instruction[28], ~Later_Instruction[27]);  // AND_Gate
  and b (b_out, Later_Instruction[31], ~Later_Instruction[30], ~Later_Instruction[29], Later_Instruction[28], ~Later_Instruction[27]);  // AND_Gate
  not not_2 (not_2_out, or_1_out);
  or or_1 (or_1_out, mov_out, not_out);
  nor nor_1 (nor_1_out, call_out, nop_out, bgt_out, beq_out, b_out);
  not not_3 (not_3_out, st_out);
  Multiplexer #(.width(4)) multiplexer_3 (
    .in0(Later_Instruction[21:18]), .in1(4'b1111), .out(multiplexer_3_out), .sel(ret_out));  // open: en
  and and_3 (and_3_out, not_3_out, Later_Instruction[26]);
  not not_4 (not_4_out, and_3_out);
  assign xnor_1_out = ~(multiplexer_2_out ^ multiplexer_3_out);  // XNOR_Gate xnor_1, 4 bits wide
  and and_4 (rs1_ans, xnor_1_out[0], xnor_1_out[1], xnor_1_out[2], xnor_1_out[3], not_2_out, and_2_out, nor_1_out);
  assign xnor_2_out = ~(multiplexer_2_out ^ multiplexer_1_out);  // XNOR_Gate xnor_2, 4 bits wide
  and and_5 (rs2_ans, xnor_2_out[0], xnor_2_out[1], xnor_2_out[2], xnor_2_out[3], not_4_out, and_2_out, nor_1_out);

  // Notes on the sheet:
  //   B
  //   A
  //   rd
  //   rs2
  //   rs1
  //   opcode
  //   rs1
  //   rd
  //   opcode
  //   I
  //   I
  //   dest
  //   hassrc1
  //   src1
  //   src2
  //   hassrc2
endmodule
